# Fritzing sketch PotentiometerStepperUno9V (saved by Fritzing 0.9.2b)

parts:
  Part1 = Arduino Uno (Rev3) - ICSP
  part = Battery block 9V
  part_2 = Rotary Potentiometer (Large) [maximum_resistance=100kΩ package=THT]
  M2 = Stepper Motor - Bipolar
  Part2 = EasyDriver_v44

nets:
  N1: Part1.A0, part_2.wiper
  5V: Part1.5V, part_2.leg1, Part2.VCC
  N2: Part1.D2, Part2.STEP
  N3: Part1.D3_PWM, Part2.DIR
  N4: Part1.D4, Part2.MS1
  N5: Part1.D5_PWM, Part2.MS2
  N6: Part1.D6_PWM, Part2.ENABLE
  GND: Part1.GND, part.-, part_2.leg2, Part2.GND
  N7: Part1.VIN, part.+, Part2.V+
  N8: M2.A, Part2.OUT2A
  N9: M2.C, Part2.OUT2B
  N10: M2.B, Part2.OUT1A
  N11: M2.D, Part2.OUT1B
